# Fritzing sketch IR_servo_Sketch (saved by Fritzing 0.8.7b)
breadboards: 1

parts:
  IR1 = TSOP312.., 314.. [package=THT]
  J1 = Basic Servo
  Part1 = Arduino Uno (Rev3) - ICSP

nets:
  N1: IR1.GND, Part1.D7
  GND: IR1.Vs, J1.gnd, Part1.GND
  VCC: IR1.Data, J1.vcc, Part1.5V
  N2: J1.pulse, Part1.D9_PWM
